// Logisim project 150117036_150117064_150117024.circ as structural Verilog: 20 circuits, main circuit main
module main (
  input  in_1,
  input  in_2,
  output [15:0] out_3,
  output [15:0] out_4,
  output [2:0] out_5,
  output [15:0] out_6,
  output [15:0] out_7,
  output [15:0] out_8,
  output [15:0] out_9,
  output [15:0] out_10,
  output [2:0] destination,
  output [2:0] out_12,
  output [1:0] out_13,
  output [15:0] out_14,
  output [15:0] out_15,
  output [15:0] out_16,
  output [1:0] out_17,
  output out_18,
  output [15:0] out_19
);

  wire ALU_OP, and_2_out, and_3_out, and_4_out, and_5_out, and_6_out, and_7_out, CLCK, CMPOP,
       controlled_buffer_1_out, counter_6_q, decoder_1_out0, decoder_1_out3, decoder_2_out0, decoder_2_out3,
       decoder_3_out0, decoder_3_out3, decoder_4_out1, decoder_4_out3, decoder_5_out0, decoder_5_out1,
       IS_ALU, IS_CMP, IS_IMM, IS_JUMP, JA, JB, JBE, JE, JEA, JUMP, jump_i, MEM_READ, MEM_WRITE,
       multiplexer_1_out, multiplexer_2_out, multiplexer_3_out, multiplexer_5_out, multiplexer_7_out,
       multiplexer_8_out, multiplexer_10_out, multiplexer_12_out, multiplexer_13_out, multiplexer_14_out,
       multiplexer_15_out, multiplexer_16_out, next, next_alu, next_cmp, next_ld, next_st, not_1_out,
       not_2_out, or_2_out, pc_enable, reg_w, reg_w_alu, reg_w_ld, REG_WRITE_ENABLED;
  wire [1:0] cmp_1_cf, counter_1_q, counter_2_q, counter_4_q, counter_5_q;
  wire [1:1] and_1_out;
  wire [2:0] OP1, SRC1;
  wire [9:0] ADDRESS10;
  wire [15:0] bit_extender_1_out, IMM_16, \input , multiplexer_4_out, rom_1_data;

  Multiplexer #(.enable("false")) multiplexer_1 (.in0(1'b0), .in1(CLCK), .out(multiplexer_1_out), .sel(IS_CMP));
  Multiplexer #(.enable("false")) multiplexer_2 (.in0(1'b0), .in1(CLCK), .out(multiplexer_2_out), .sel(or_2_out));
  assign controlled_buffer_1_out = pc_enable ? multiplexer_2_out : 1'bz;  // Controlled_Buffer controlled_buffer_1
  or or_1 (CMPOP, JEA, JA, JE, JB, JBE);
  Multiplexer #(.enable("false")) multiplexer_3 (.in0(1'b0), .in1(CLCK), .out(multiplexer_3_out), .sel(IS_ALU));
  Counter #(.width(2), .max('h3)) counter_1 (
    .Q(counter_1_q), .clk(multiplexer_1_out));  // open: load, D, count, carry, clr
  Multiplexer #(.width(16), .enable("false")) multiplexer_4 (
    .in0(out_3), .in1(out_7), .out(multiplexer_4_out), .sel(MEM_READ));
  Multiplexer #(.enable("false")) multiplexer_5 (
    .in0(1'b0), .in1(REG_WRITE_ENABLED), .out(multiplexer_5_out), .sel(reg_w));
  or or_2 (or_2_out, next, jump_i);
  Counter #(.width(2), .max('h3)) counter_2 (
    .Q(counter_2_q), .clk(multiplexer_3_out));  // open: load, D, count, carry, clr
  Decoder #(.select(2)) decoder_1 (
    .out0(decoder_1_out0), .out3(decoder_1_out3), .sel(counter_1_q));  // open: out1, out2, en
  and and_1 (and_1_out[1], out_18, CMPOP);
  Decoder #(.select(2)) decoder_2 (
    .out0(decoder_2_out0), .out1(reg_w_alu), .out3(decoder_2_out3), .sel(counter_2_q));  // open: out2, en
  assign next_cmp = decoder_1_out0 ? 1'b0 : 1'bz;  // Controlled_Buffer controlled_buffer_2
  assign next_cmp = decoder_1_out3 ? 1'b1 : 1'bz;  // Controlled_Buffer controlled_buffer_3
  assign next_alu = decoder_2_out0 ? 1'b0 : 1'bz;  // Controlled_Buffer controlled_buffer_4
  assign next_alu = decoder_2_out3 ? 1'b1 : 1'bz;  // Controlled_Buffer controlled_buffer_5
  Register_File register_file_1 (
    .Input_data(multiplexer_4_out), .write_source__register(destination), .Write_Enable(multiplexer_5_out),
    .clck(CLCK), .Register_1_Data(out_4), .Register_2_Data(out_9), .Input_Reg1(out_5), .Input_Reg2(out_12),
    .clear(in_1));
  counter counter_3 (
    .next(next), .jump(jump_i), .clk(controlled_buffer_1_out), .\input (\input ), .reset(in_2),
    .\output (out_16), .value_to_load(out_19));
  assign bit_extender_1_out = {{6{ADDRESS10[9]}}, ADDRESS10};  // Bit_Extender bit_extender_1
  Multiplexer #(.select(2), .width(16), .enable("false")) multiplexer_6 (
    .in0(16'h1), .in1(bit_extender_1_out), .in2(bit_extender_1_out), .in3(16'h1), .out(\input ),
    .sel({and_1_out[1], JUMP}));
  ROM #(.addrWidth(16), .dataWidth(16)) rom_1 (.addr(out_16), .data(rom_1_data), .sel(1'b1));
  Multiplexer #(.enable("false")) multiplexer_7 (.in0(1'b0), .in1(CLCK), .out(multiplexer_7_out), .sel(MEM_READ));
  Multiplexer #(.enable("false")) multiplexer_8 (.in0(1'b0), .in1(CLCK), .out(multiplexer_8_out), .sel(IS_JUMP));
  Clock clock_1 (.out(CLCK));
  Counter #(.width(2), .max('h3)) counter_4 (
    .Q(counter_4_q), .clk(multiplexer_7_out));  // open: load, D, count, carry, clr
  Counter #(.width(2), .max('h3)) counter_5 (
    .Q(counter_5_q), .clk(multiplexer_8_out));  // open: load, D, count, carry, clr
  CPU cpu_1 (
    .Assembly(rom_1_data), .IMM_SIGNAL(IS_IMM), .DEST___ST_SRC1___JUMPCODE(destination), .SRC1(SRC1),
    .SRC2___OP2(out_12), .OP1(OP1), .ALU_OP(ALU_OP), .ADDRESS(ADDRESS10), .is_cmp(IS_CMP), .IMM_16(IMM_16),
    .MemRead(MEM_READ), .MemWrite(MEM_WRITE), .is_alu(IS_ALU), .register_write_enable(REG_WRITE_ENABLED),
    .is_jump(IS_JUMP));
  Decoder #(.select(2)) decoder_3 (
    .out0(decoder_3_out0), .out1(reg_w_ld), .out3(decoder_3_out3), .sel(counter_4_q));  // open: out2, en
  Decoder #(.select(2), .enable("false")) decoder_4 (
    .out1(decoder_4_out1), .out3(decoder_4_out3), .sel(counter_5_q));  // open: out0, out2
  ALU alu_1 (.c_in(1'b0), .Result_of_operation(out_8), .A(out_4), .B(out_10), .ALU_OPERATION(ALU_OP));  // open: c_out
  assign jump_i = decoder_4_out1 ? 1'b1 : 1'bz;  // Controlled_Buffer controlled_buffer_6
  assign jump_i = decoder_4_out3 ? 1'b0 : 1'bz;  // Controlled_Buffer controlled_buffer_7
  assign next_ld = decoder_3_out0 ? 1'b0 : 1'bz;  // Controlled_Buffer controlled_buffer_8
  assign next_ld = decoder_3_out3 ? 1'b1 : 1'bz;  // Controlled_Buffer controlled_buffer_9
  assign out_3 = IS_ALU ? out_8 : 16'bz;  // Controlled_Buffer controlled_buffer_10
  Multiplexer #(.select(2), .width(3), .enable("false")) multiplexer_9 (
    .in0(SRC1), .in1(OP1), .in2(destination), .out(out_5), .sel({MEM_WRITE, IS_CMP}));  // open: in3
  CMP cmp_1 (.in_1(out_4), .in_2(out_9), .CF(cmp_1_cf[0]), .ZF(cmp_1_cf[1]));
  Counter #(.width(1), .max('h1)) counter_6 (
    .Q(counter_6_q), .clk(multiplexer_10_out));  // open: load, D, count, carry, clr
  Multiplexer #(.enable("false")) multiplexer_10 (.in0(1'b0), .in1(CLCK), .out(multiplexer_10_out), .sel(MEM_WRITE));
  RAM #(.addrWidth(10), .dataWidth(16), .bus("separate")) ram_1 (
    .addr(ADDRESS10), .din(out_4), .data(out_7), .str(MEM_WRITE), .sel(1'b1), .clk(CLCK), .ld(MEM_READ),
    .clr(1'b0));
  Register #(.width(2)) register_1 (.D(cmp_1_cf), .Q(out_13), .clk(CLCK));  // open: en, clr
  Multiplexer #(.width(16), .enable("false")) multiplexer_11 (.in0(out_9), .in1(IMM_16), .out(out_10), .sel(and_2_out));
  and and_2 (and_2_out, IS_IMM, IS_ALU);
  Decoder decoder_5 (.out0(decoder_5_out0), .out1(decoder_5_out1), .sel(counter_6_q));  // open: en
  assign next_st = decoder_5_out0 ? 1'b0 : 1'bz;  // Controlled_Buffer controlled_buffer_11
  assign next_st = decoder_5_out1 ? 1'b1 : 1'bz;  // Controlled_Buffer controlled_buffer_12
  or or_3 (reg_w, reg_w_alu, reg_w_ld);
  Decoder #(.select(3)) decoder_6 (
    .out0(JUMP), .out1(JE), .out2(JA), .out3(JB), .out4(JBE), .out5(JEA), .sel(destination), .en(IS_JUMP));  // open: out6, out7
  or or_4 (next, next_alu, next_ld, next_cmp, next_st);
  or or_5 (pc_enable, next_alu, next_ld, next_cmp, next_st, jump_i);
  not not_1 (not_1_out, out_13[0]);
  not not_2 (not_2_out, out_13[1]);
  Multiplexer #(.enable("false")) multiplexer_12 (.in0(1'b0), .in1(not_1_out), .out(multiplexer_12_out), .sel(IS_JUMP));
  Multiplexer #(.enable("false")) multiplexer_13 (.in0(1'b0), .in1(not_2_out), .out(multiplexer_13_out), .sel(IS_JUMP));
  Multiplexer #(.enable("false")) multiplexer_14 (.in0(1'b0), .in1(out_13[0]), .out(multiplexer_14_out), .sel(IS_JUMP));
  Multiplexer #(.enable("false")) multiplexer_15 (.in0(1'b0), .in1(out_13[0]), .out(multiplexer_15_out), .sel(IS_JUMP));
  Multiplexer #(.enable("false")) multiplexer_16 (.in0(1'b0), .in1(out_13[1]), .out(multiplexer_16_out), .sel(IS_JUMP));
  and and_3 (and_3_out, JEA, multiplexer_12_out);
  and and_4 (and_4_out, JA, multiplexer_12_out, multiplexer_13_out);
  and and_5 (and_5_out, JE, multiplexer_12_out, multiplexer_13_out);
  and and_6 (and_6_out, JB, multiplexer_14_out, multiplexer_13_out);
  and and_7 (and_7_out, JBE, multiplexer_15_out, multiplexer_16_out);
  or or_6 (out_18, and_3_out, and_4_out, and_5_out, and_6_out, and_7_out);

  assign out_6 = out_4;
  assign out_14 = out_4;
  assign out_15 = out_7;
  assign out_17 = out_13;

  // Other names for the same wires on the sheet: alu_Result[15:0] = out_8; ALU_second_input[15:0] = out_10;
  //   CF_ZF[1:0] = out_13; clear = in_1; cmpsc = out_18; data_out[15:0] = out_7;
  //   DEST___SRC_1___JUMPCODE[2:0] = destination; pc_enable_alu = next_alu; pc_enable_cmp = next_cmp;
  //   pc_enable_jump = jump_i; pc_enable_ld = next_ld; pc_enable_st = next_st; read_register_1[2:0] = out_5;
  //   read_register_2[2:0] = out_12; SRC2___OP2[2:0] = out_12; reg1_value[15:0] = out_4; reg2_value[15:0] = out_9;
  //   register_write_data[15:0] = out_3

  // Notes on the sheet:
  //   data kısmı aludan gelecek olan sonuca göre yazılacak
  //   CMP FSM
  //   ALU FSM
  //   contents of rom_1 (hex, n*v repeats v):
  //   6005 6404 2880 8c00 9001 9402 1982 5f28 a003 a404 a805 b806 bc07 6003 c004 e803 effd 2000 7205 c025
  //   effd e403 2000 2000 b009 e00a 9*2000 7f84 c03e effe f47c
  //   LD FSM
  //   JUMP FSM
  //   CFsağdaki , ZF soldaki
  //   IMM or not
  //   SRC1 Register
  //   OP1 Register
  //   CMP or not
  //   LD
  //   ST
  //   JUMP
  //   SRC2/OP2 Register
  //   0-And , 1-Add
  //   Jump,ST,LD address
  //   extended 16 bit IMM value
  //   ALU operation yapılacaksa 1 dönecek
  //   Dest for alu operations and load 
  //   SRC1 for ST
  //   ALU veya LD ise 1 dönecek
  //   ST FSM
endmodule

module CPU (
  input  [15:0] Assembly,
  output IMM_SIGNAL,
  output [2:0] DEST___ST_SRC1___JUMPCODE,
  output [2:0] SRC1,
  output [2:0] SRC2___OP2,
  output [2:0] OP1,
  output ALU_OP,
  output [9:0] ADDRESS,
  output is_cmp,
  output [15:0] IMM_16,
  output MemRead,
  output MemWrite,
  output is_alu,
  output register_write_enable,
  output is_jump
);

  wire ADD, ADDI, AND, ANDI, or_1_out, or_2_out;

  assign IMM_16 = {{9{1'b0}}, Assembly[6:0]};  // Bit_Extender bit_extender_1
  Decoder #(.select(3), .enable("false")) decoder_1 (
    .out0(AND), .out1(ADD), .out2(ANDI), .out3(ADDI), .out4(MemRead), .out5(MemWrite), .out6(is_cmp),
    .out7(is_jump), .sel(Assembly[15:13]));
  or or_1 (or_1_out, AND, ANDI);
  or or_2 (or_2_out, ADD, ADDI);
  Priority_Encoder #(.select(1)) priority_encoder_1 (
    .in0(or_1_out), .in1(or_2_out), .out(ALU_OP));  // open: gs, en_out, en_in
  or or_3 (is_alu, ADDI, ADD, ANDI, AND);
  or or_4 (register_write_enable, is_alu, MemRead);
  or or_5 (IMM_SIGNAL, ADDI, ANDI);

  assign ADDRESS = Assembly[9:0];
  assign DEST___ST_SRC1___JUMPCODE = Assembly[12:10];
  assign OP1 = Assembly[5:3];
  assign SRC1 = Assembly[9:7];
  assign SRC2___OP2 = Assembly[2:0];

  // Other names for the same wires on the sheet: ALU_CONTROL = is_alu; ALU_OPERATION = ALU_OP; CMP = is_cmp;
  //   IMM[6:0] = Assembly[6:0]; OP2[2:0] = Assembly[2:0]; SRC2[2:0] = Assembly[2:0]; JMP = is_jump; LD = MemRead;
  //   OPCODE[2:0] = Assembly[15:13]; ST = MemWrite; DEST[2:0] = Assembly[12:10]; JumpCode[2:0] = Assembly[12:10];
  //   ST_SRC1[2:0] = Assembly[12:10]

  // Notes on the sheet:
  //   ALU operation yapılacaksa 1 dönecek
  //   ALU operation yapılacaksa 1 dönecek
  //   AND ve ADD i ayırmak için kullanacagız
  //   ALU veya LD ise 1 dönecek
endmodule

module Register_File (
  input  [15:0] Input_data,
  input  [2:0] write_source__register,
  input  Write_Enable,
  input  clear,
  input  clck,
  input  [2:0] Input_Reg1,
  input  [2:0] Input_Reg2,
  output [15:0] Register_1_Data,
  output [15:0] Register_2_Data
);

  wire and_1_out, and_2_out, and_3_out, and_4_out, and_5_out, and_6_out, and_7_out, and_8_out,
       decoder_1_out0, decoder_1_out1, decoder_1_out2, decoder_1_out3, decoder_1_out4, decoder_1_out5,
       decoder_1_out6, decoder_1_out7;
  wire [15:0] n16bit_register_1_out_5, n16bit_register_2_out_5, n16bit_register_3_out_5,
       n16bit_register_4_out_5, n16bit_register_5_out_5, n16bit_register_6_out_5, n16bit_register_7_out_5,
       n16bit_register_8_out_5;

  Decoder #(.select(3)) decoder_1 (
    .out0(decoder_1_out0), .out1(decoder_1_out1), .out2(decoder_1_out2), .out3(decoder_1_out3),
    .out4(decoder_1_out4), .out5(decoder_1_out5), .out6(decoder_1_out6), .out7(decoder_1_out7),
    .sel(write_source__register));  // open: en
  and and_1 (and_1_out, decoder_1_out0, Write_Enable);
  and and_2 (and_2_out, decoder_1_out1, Write_Enable);
  and and_3 (and_3_out, decoder_1_out2, Write_Enable);
  and and_4 (and_4_out, decoder_1_out3, Write_Enable);
  and and_5 (and_5_out, decoder_1_out4, Write_Enable);
  and and_6 (and_6_out, decoder_1_out5, Write_Enable);
  and and_7 (and_7_out, decoder_1_out6, Write_Enable);
  and and_8 (and_8_out, decoder_1_out7, Write_Enable);
  _16bit_register u_16bit_register_1 (
    .enable(and_1_out), .clear(clear), .clk(clck), .Input(Input_data), .out_5(n16bit_register_1_out_5));
  _16bit_register u_16bit_register_2 (
    .enable(and_2_out), .clear(clear), .clk(clck), .Input(Input_data), .out_5(n16bit_register_2_out_5));
  _16bit_register u_16bit_register_3 (
    .enable(and_3_out), .clear(clear), .clk(clck), .Input(Input_data), .out_5(n16bit_register_3_out_5));
  _16bit_register u_16bit_register_4 (
    .enable(and_4_out), .clear(clear), .clk(clck), .Input(Input_data), .out_5(n16bit_register_4_out_5));
  _16bit_register u_16bit_register_5 (
    .enable(and_5_out), .clear(clear), .clk(clck), .Input(Input_data), .out_5(n16bit_register_5_out_5));
  _16bit_register u_16bit_register_6 (
    .enable(and_6_out), .clear(clear), .clk(clck), .Input(Input_data), .out_5(n16bit_register_6_out_5));
  _16bit_register u_16bit_register_7 (
    .enable(and_7_out), .clear(clear), .clk(clck), .Input(Input_data), .out_5(n16bit_register_7_out_5));
  _16bit_register u_16bit_register_8 (
    .enable(and_8_out), .clear(clear), .clk(clck), .Input(Input_data), .out_5(n16bit_register_8_out_5));
  Multiplexer #(.select(3), .width(16), .enable("false")) multiplexer_1 (
    .in0(n16bit_register_1_out_5), .in1(n16bit_register_2_out_5), .in2(n16bit_register_3_out_5),
    .in3(n16bit_register_4_out_5), .in4(n16bit_register_5_out_5), .in5(n16bit_register_6_out_5),
    .in6(n16bit_register_7_out_5), .in7(n16bit_register_8_out_5), .out(Register_1_Data), .sel(Input_Reg1));
  Multiplexer #(.select(3), .width(16), .enable("false")) multiplexer_2 (
    .in0(n16bit_register_1_out_5), .in1(n16bit_register_2_out_5), .in2(n16bit_register_3_out_5),
    .in3(n16bit_register_4_out_5), .in4(n16bit_register_5_out_5), .in5(n16bit_register_6_out_5),
    .in6(n16bit_register_7_out_5), .in7(n16bit_register_8_out_5), .out(Register_2_Data), .sel(Input_Reg2));
endmodule

module ALU (
  input  [15:0] A,
  input  [15:0] B,
  input  c_in,
  input  ALU_OPERATION,
  output c_out,
  output [15:0] Result_of_operation
);

  wire not_1_out;
  wire [15:0] _16bit_and_out, n16bit_adde_1_sum;

  _16bit_adde u_16bit_adde_1 (.c_in(c_in), .A(A), .B(B), .sum(n16bit_adde_1_sum), .c_out(c_out));
  assign _16bit_and_out = A & B;  // AND_Gate _16bit_and, 16 bits wide
  not not_1 (not_1_out, ALU_OPERATION);
  Multiplexer #(.width(16), .enable("false")) multiplexer_1 (
    .in0(n16bit_adde_1_sum), .in1(_16bit_and_out), .out(Result_of_operation), .sel(not_1_out));
endmodule

module counter (
  input  next,
  input  jump,
  input  clk,
  input  [15:0] \input ,
  input  reset,
  output [15:0] value_to_load,
  output [15:0] \output 
);

  wire _16bit_adder_p4, load_enable, not_1_out;

  not not_1 (not_1_out, next);
  and and_1 (load_enable, not_1_out, jump);
  Counter #(.width(16), .max('hffff)) counter_1 (
    .load(load_enable), .D(value_to_load), .count(next), .Q(\output ), .clk(clk), .clr(reset));  // open: carry
  // _16bit_adde _16bit_adder: pin names not known; wires that end beside it: \input , \output , value_to_load, _16bit_adder_p4, 1'b0, _16bit_adder_p4

  // Other names for the same wires on the sheet: count = next

  // Notes on the sheet:
  //   increment by 1 (count=1, clock ticks)
endmodule

module CMP (
  input  [15:0] in_1,
  input  [15:0] in_2,
  output CF,
  output ZF
);

  wire GE, GT, LE, n16bit_comparator_1_eq, n16bit_comparator_1_gt, n16bit_comparator_1_lt, not_1_out,
       not_2_out, not_3_out, not_4_out;

  _16bit_comparator u_16bit_comparator_1 (
    .A(in_1), .B(in_2), .GT(n16bit_comparator_1_gt), .EQ(n16bit_comparator_1_eq), .LT(n16bit_comparator_1_lt));
  not not_1 (not_1_out, n16bit_comparator_1_eq);
  not not_2 (not_2_out, n16bit_comparator_1_gt);
  not not_3 (not_3_out, n16bit_comparator_1_lt);
  not not_4 (not_4_out, n16bit_comparator_1_eq);
  or or_1 (GE, n16bit_comparator_1_gt, n16bit_comparator_1_eq);
  and and_1 (GT, n16bit_comparator_1_gt, not_1_out);
  and and_2 (ZF, not_2_out, n16bit_comparator_1_eq, not_3_out);
  and and_3 (CF, not_4_out, n16bit_comparator_1_lt);
  or or_2 (LE, n16bit_comparator_1_eq, n16bit_comparator_1_lt);

  // Other names for the same wires on the sheet: E = ZF; LT = CF

  // Notes on the sheet:
  //   if LE -> 1 , CF=1 , if LE->0 so OP1>=OP2 , CF=0
  //   OP1 > OP2 -> CF0 ZF0
  //   OP1 = OP2 -> CF0 ZF1
  //   OP1 < OP2 -> CF1 ZF0
  //   OP1 <= OP2 -> CF1 ZF1
  //   OP1 >= OP2 -> CF=0 , ZF not important
endmodule

module half_adder (
  input  A,
  input  B,
  output sum,
  output c_out
);

  xor xor_1 (sum, A, B);
  and and_1 (c_out, A, B);
endmodule

module full_adder (
  input  A,
  input  B,
  input  c_in,
  output sum,
  output c_out
);

  wire and_1_out, and_2_out, xor_1_out;

  xor xor_1 (xor_1_out, A, B);
  xor xor_2 (sum, xor_1_out, c_in);
  and and_1 (and_1_out, xor_1_out, c_in);
  and and_2 (and_2_out, B, A);
  or or_1 (c_out, and_1_out, and_2_out);
endmodule

module _2bit_adder (
  input  [1:0] A,
  input  [1:0] B,
  input  c_in,
  output [1:0] sum,
  output c_out
);

  wire full_adder_1_c_out;

  full_adder full_adder_1 (.A(A[0]), .B(B[0]), .c_in(c_in), .sum(sum[0]), .c_out(full_adder_1_c_out));
  full_adder full_adder_2 (.A(A[1]), .B(B[1]), .c_in(full_adder_1_c_out), .sum(sum[1]), .c_out(c_out));
endmodule

// c_in
module _4bit_adder (
  input  [3:0] A,
  input  [3:0] B,
  input  in_3,
  output [3:0] sum,
  output c_out
);

  wire n2bit_adder_1_c_out;

  _2bit_adder u_2bit_adder_1 (.c_in(in_3), .A(A[1:0]), .B(B[1:0]), .sum(sum[1:0]), .c_out(n2bit_adder_1_c_out));
  _2bit_adder u_2bit_adder_2 (.c_in(n2bit_adder_1_c_out), .A(A[3:2]), .B(B[3:2]), .sum(sum[3:2]), .c_out(c_out));
endmodule

module _8bit_adder (
  input  [7:0] A,
  input  [7:0] B,
  input  c_in,
  output [7:0] sum,
  output c_out
);

  wire n4bit_adder_1_c_out;

  _4bit_adder u_4bit_adder_1 (.in_3(c_in), .A(A[3:0]), .B(B[3:0]), .sum(sum[3:0]), .c_out(n4bit_adder_1_c_out));
  _4bit_adder u_4bit_adder_2 (.in_3(n4bit_adder_1_c_out), .A(A[7:4]), .B(B[7:4]), .sum(sum[7:4]), .c_out(c_out));
endmodule

module _16bit_adde (
  input  [15:0] A,
  input  [15:0] B,
  input  c_in,
  output [15:0] sum,
  output c_out
);

  wire n8bit_adder_1_c_out;

  _8bit_adder u_8bit_adder_1 (.c_in(c_in), .A(A[7:0]), .B(B[7:0]), .sum(sum[7:0]), .c_out(n8bit_adder_1_c_out));
  _8bit_adder u_8bit_adder_2 (.c_in(n8bit_adder_1_c_out), .A(A[15:8]), .B(B[15:8]), .sum(sum[15:8]), .c_out(c_out));
endmodule

module _16bit_register (
  input  [15:0] Input,
  input  enable,
  input  clear,
  input  clk,
  output [15:0] out_5
);

  wire multiplexer_1_out, multiplexer_2_out, multiplexer_3_out, multiplexer_4_out, multiplexer_5_out,
       multiplexer_6_out, multiplexer_7_out, multiplexer_8_out, multiplexer_9_out, multiplexer_10_out,
       multiplexer_11_out, multiplexer_12_out, multiplexer_13_out, multiplexer_14_out, multiplexer_15_out,
       multiplexer_16_out;
  wire [0:0] not_1_out;

  not not_1 (not_1_out[0], enable);
  Multiplexer #(.select(2), .enable("false")) multiplexer_1 (
    .in0(Input[15]), .in1(out_5[15]), .in2(1'b0), .in3(1'b0), .out(multiplexer_1_out),
    .sel({clear, not_1_out[0]}));
  Multiplexer #(.select(2), .enable("false")) multiplexer_2 (
    .in0(Input[14]), .in1(out_5[14]), .in2(1'b0), .in3(1'b0), .out(multiplexer_2_out),
    .sel({clear, not_1_out[0]}));
  d_flip_flop d_flip_flop_1 (.D(multiplexer_1_out), .clk(clk), .Q(out_5[15]));
  Multiplexer #(.select(2), .enable("false")) multiplexer_3 (
    .in0(Input[13]), .in1(out_5[13]), .in2(1'b0), .in3(1'b0), .out(multiplexer_3_out),
    .sel({clear, not_1_out[0]}));
  d_flip_flop d_flip_flop_2 (.D(multiplexer_2_out), .clk(clk), .Q(out_5[14]));
  Multiplexer #(.select(2), .enable("false")) multiplexer_4 (
    .in0(Input[12]), .in1(out_5[12]), .in2(1'b0), .in3(1'b0), .out(multiplexer_4_out),
    .sel({clear, not_1_out[0]}));
  d_flip_flop d_flip_flop_3 (.D(multiplexer_3_out), .clk(clk), .Q(out_5[13]));
  Multiplexer #(.select(2), .enable("false")) multiplexer_5 (
    .in0(Input[11]), .in1(out_5[11]), .in2(1'b0), .in3(1'b0), .out(multiplexer_5_out),
    .sel({clear, not_1_out[0]}));
  d_flip_flop d_flip_flop_4 (.D(multiplexer_4_out), .clk(clk), .Q(out_5[12]));
  Multiplexer #(.select(2), .enable("false")) multiplexer_6 (
    .in0(Input[10]), .in1(out_5[10]), .in2(1'b0), .in3(1'b0), .out(multiplexer_6_out),
    .sel({clear, not_1_out[0]}));
  d_flip_flop d_flip_flop_5 (.D(multiplexer_5_out), .clk(clk), .Q(out_5[11]));
  Multiplexer #(.select(2), .enable("false")) multiplexer_7 (
    .in0(Input[9]), .in1(out_5[9]), .in2(1'b0), .in3(1'b0), .out(multiplexer_7_out),
    .sel({clear, not_1_out[0]}));
  d_flip_flop d_flip_flop_6 (.D(multiplexer_6_out), .clk(clk), .Q(out_5[10]));
  Multiplexer #(.select(2), .enable("false")) multiplexer_8 (
    .in0(Input[8]), .in1(out_5[8]), .in2(1'b0), .in3(1'b0), .out(multiplexer_8_out),
    .sel({clear, not_1_out[0]}));
  d_flip_flop d_flip_flop_7 (.D(multiplexer_7_out), .clk(clk), .Q(out_5[9]));
  Multiplexer #(.select(2), .enable("false")) multiplexer_9 (
    .in0(Input[7]), .in1(out_5[7]), .in2(1'b0), .in3(1'b0), .out(multiplexer_9_out),
    .sel({clear, not_1_out[0]}));
  d_flip_flop d_flip_flop_8 (.D(multiplexer_8_out), .clk(clk), .Q(out_5[8]));
  Multiplexer #(.select(2), .enable("false")) multiplexer_10 (
    .in0(Input[6]), .in1(out_5[6]), .in2(1'b0), .in3(1'b0), .out(multiplexer_10_out),
    .sel({clear, not_1_out[0]}));
  d_flip_flop d_flip_flop_9 (.D(multiplexer_9_out), .clk(clk), .Q(out_5[7]));
  Multiplexer #(.select(2), .enable("false")) multiplexer_11 (
    .in0(Input[5]), .in1(out_5[5]), .in2(1'b0), .in3(1'b0), .out(multiplexer_11_out),
    .sel({clear, not_1_out[0]}));
  d_flip_flop d_flip_flop_10 (.D(multiplexer_10_out), .clk(clk), .Q(out_5[6]));
  Multiplexer #(.select(2), .enable("false")) multiplexer_12 (
    .in0(Input[4]), .in1(out_5[4]), .in2(1'b0), .in3(1'b0), .out(multiplexer_12_out),
    .sel({clear, not_1_out[0]}));
  d_flip_flop d_flip_flop_11 (.D(multiplexer_11_out), .clk(clk), .Q(out_5[5]));
  Multiplexer #(.select(2), .enable("false")) multiplexer_13 (
    .in0(Input[3]), .in1(out_5[3]), .in2(1'b0), .in3(1'b0), .out(multiplexer_13_out),
    .sel({clear, not_1_out[0]}));
  d_flip_flop d_flip_flop_12 (.D(multiplexer_12_out), .clk(clk), .Q(out_5[4]));
  Multiplexer #(.select(2), .enable("false")) multiplexer_14 (
    .in0(Input[2]), .in1(out_5[2]), .in2(1'b0), .in3(1'b0), .out(multiplexer_14_out),
    .sel({clear, not_1_out[0]}));
  d_flip_flop d_flip_flop_13 (.D(multiplexer_13_out), .clk(clk), .Q(out_5[3]));
  Multiplexer #(.select(2), .enable("false")) multiplexer_15 (
    .in0(Input[1]), .in1(out_5[1]), .in2(1'b0), .in3(1'b0), .out(multiplexer_15_out),
    .sel({clear, not_1_out[0]}));
  d_flip_flop d_flip_flop_14 (.D(multiplexer_14_out), .clk(clk), .Q(out_5[2]));
  Multiplexer #(.select(2), .enable("false")) multiplexer_16 (
    .in0(Input[0]), .in1(out_5[0]), .in2(1'b0), .in3(1'b0), .out(multiplexer_16_out),
    .sel({clear, not_1_out[0]}));
  d_flip_flop d_flip_flop_15 (.D(multiplexer_15_out), .clk(clk), .Q(out_5[1]));
  d_flip_flop d_flip_flop_16 (.D(multiplexer_16_out), .clk(clk), .Q(out_5[0]));
endmodule

module d_latch (
  input  D,
  input  c,
  output Q
);

  wire and_1_out, and_2_out, half_adder_1_c_out, half_adder_1_sum, multiplexer_1_out, nand_1_out, nor_1_out,
       not_1_out, register_1_q;

  not not_1 (not_1_out, D);
  half_adder half_adder_1 (.A(c), .B(register_1_q), .sum(half_adder_1_sum), .c_out(half_adder_1_c_out));
  and and_1 (and_1_out, D, c);
  and and_2 (and_2_out, c, not_1_out);
  Register #(.width(1)) register_1 (.D(nand_1_out), .en(1'b1), .Q(register_1_q), .clk(c));  // open: clr
  nand nand_1 (nand_1_out, half_adder_1_sum, half_adder_1_c_out);
  nor nor_1 (nor_1_out, and_1_out, Q);
  nor nor_2 (Q, multiplexer_1_out, and_2_out);
  Multiplexer #(.enable("false")) multiplexer_1 (
    .in0(1'b1), .in1(nor_1_out), .out(multiplexer_1_out), .sel(register_1_q));
endmodule

module d_flip_flop (
  input  D,
  input  clk,
  output Q
);

  wire d_latch_1_q, not_1_out;

  d_latch d_latch_1 (.D(D), .c(not_1_out), .Q(d_latch_1_q));
  not not_1 (not_1_out, clk);
  d_latch d_latch_2 (.D(d_latch_1_q), .c(clk), .Q(Q));
endmodule

module half_comparator (
  input  A,
  input  B,
  output gt,
  output eq,
  output lt
);

  wire and_1_out, and_2_out, not_1_out, not_2_out, not_3_out, not_4_out;

  not not_1 (not_1_out, B);
  not not_2 (not_2_out, A);
  and and_1 (and_1_out, A, B);
  not not_3 (not_3_out, A);
  and and_2 (and_2_out, not_3_out, not_4_out);
  not not_4 (not_4_out, B);
  and and_3 (gt, A, not_1_out);
  and and_4 (lt, not_2_out, B);
  or or_1 (eq, and_1_out, and_2_out);
endmodule

module full_comparator (
  input  a,
  input  b,
  input  gt_in,
  input  eq_in,
  input  lt_in,
  output gt,
  output eq,
  output lt
);

  wire and_1_out, and_2_out, and_3_out, and_4_out, and_5_out, and_6_out, not_1_out, not_2_out, not_3_out,
       not_4_out, or_1_out;

  not not_1 (not_1_out, a);
  not not_2 (not_2_out, b);
  and and_1 (and_1_out, a, not_3_out);
  not not_3 (not_3_out, b);
  not not_4 (not_4_out, a);
  and and_2 (and_2_out, not_4_out, b);
  and and_3 (and_3_out, a, b);
  or or_1 (or_1_out, and_3_out, and_4_out);
  and and_4 (and_4_out, not_1_out, not_2_out);
  and and_5 (and_5_out, and_1_out, eq_in);
  and and_6 (and_6_out, eq_in, and_2_out);
  and and_7 (eq, eq_in, or_1_out);
  or or_2 (gt, and_5_out, gt_in);
  or or_3 (lt, and_6_out, lt_in);
endmodule

module _16bit_comparator (
  input  [15:0] A,
  input  [15:0] B,
  output GT,
  output EQ,
  output LT
);

  wire full_comparator_1_eq, full_comparator_1_gt, full_comparator_1_lt, full_comparator_2_eq,
       full_comparator_2_gt, full_comparator_2_lt, full_comparator_3_eq, full_comparator_3_gt,
       full_comparator_3_lt, full_comparator_4_eq, full_comparator_4_gt, full_comparator_4_lt,
       full_comparator_5_eq, full_comparator_5_gt, full_comparator_5_lt, full_comparator_6_eq,
       full_comparator_6_gt, full_comparator_6_lt, full_comparator_7_eq, full_comparator_7_gt,
       full_comparator_7_lt, full_comparator_8_eq, full_comparator_8_gt, full_comparator_8_lt,
       full_comparator_9_eq, full_comparator_9_gt, full_comparator_9_lt, full_comparator_10_eq,
       full_comparator_10_gt, full_comparator_10_lt, full_comparator_11_eq, full_comparator_11_gt,
       full_comparator_11_lt, full_comparator_12_eq, full_comparator_12_gt, full_comparator_12_lt,
       full_comparator_13_eq, full_comparator_13_gt, full_comparator_13_lt, full_comparator_14_eq,
       full_comparator_14_gt, full_comparator_14_lt, half_comparator_1_eq, half_comparator_1_gt,
       half_comparator_1_lt;

  half_comparator half_comparator_1 (
    .A(A[15]), .B(B[15]), .gt(half_comparator_1_gt), .eq(half_comparator_1_eq), .lt(half_comparator_1_lt));
  full_comparator full_comparator_1 (
    .a(A[14]), .b(B[14]), .gt_in(half_comparator_1_gt), .eq_in(half_comparator_1_eq),
    .lt_in(half_comparator_1_lt), .gt(full_comparator_1_gt), .eq(full_comparator_1_eq),
    .lt(full_comparator_1_lt));
  full_comparator full_comparator_2 (
    .a(A[6]), .b(B[6]), .gt_in(full_comparator_3_gt), .eq_in(full_comparator_3_eq),
    .lt_in(full_comparator_3_lt), .gt(full_comparator_2_gt), .eq(full_comparator_2_eq),
    .lt(full_comparator_2_lt));
  full_comparator full_comparator_3 (
    .a(A[7]), .b(B[7]), .gt_in(full_comparator_12_gt), .eq_in(full_comparator_12_eq),
    .lt_in(full_comparator_12_lt), .gt(full_comparator_3_gt), .eq(full_comparator_3_eq),
    .lt(full_comparator_3_lt));
  full_comparator full_comparator_4 (
    .a(A[12]), .b(B[12]), .gt_in(full_comparator_5_gt), .eq_in(full_comparator_5_eq),
    .lt_in(full_comparator_5_lt), .gt(full_comparator_4_gt), .eq(full_comparator_4_eq),
    .lt(full_comparator_4_lt));
  full_comparator full_comparator_5 (
    .a(A[13]), .b(B[13]), .gt_in(full_comparator_1_gt), .eq_in(full_comparator_1_eq),
    .lt_in(full_comparator_1_lt), .gt(full_comparator_5_gt), .eq(full_comparator_5_eq),
    .lt(full_comparator_5_lt));
  full_comparator full_comparator_6 (
    .a(A[5]), .b(B[5]), .gt_in(full_comparator_2_gt), .eq_in(full_comparator_2_eq),
    .lt_in(full_comparator_2_lt), .gt(full_comparator_6_gt), .eq(full_comparator_6_eq),
    .lt(full_comparator_6_lt));
  full_comparator full_comparator_7 (
    .a(A[11]), .b(B[11]), .gt_in(full_comparator_4_gt), .eq_in(full_comparator_4_eq),
    .lt_in(full_comparator_4_lt), .gt(full_comparator_7_gt), .eq(full_comparator_7_eq),
    .lt(full_comparator_7_lt));
  full_comparator full_comparator_8 (
    .a(A[4]), .b(B[4]), .gt_in(full_comparator_6_gt), .eq_in(full_comparator_6_eq),
    .lt_in(full_comparator_6_lt), .gt(full_comparator_8_gt), .eq(full_comparator_8_eq),
    .lt(full_comparator_8_lt));
  full_comparator full_comparator_9 (
    .a(A[10]), .b(B[10]), .gt_in(full_comparator_7_gt), .eq_in(full_comparator_7_eq),
    .lt_in(full_comparator_7_lt), .gt(full_comparator_9_gt), .eq(full_comparator_9_eq),
    .lt(full_comparator_9_lt));
  full_comparator full_comparator_10 (
    .a(A[2]), .b(B[2]), .gt_in(full_comparator_11_gt), .eq_in(full_comparator_11_eq),
    .lt_in(full_comparator_11_lt), .gt(full_comparator_10_gt), .eq(full_comparator_10_eq),
    .lt(full_comparator_10_lt));
  full_comparator full_comparator_11 (
    .a(A[3]), .b(B[3]), .gt_in(full_comparator_8_gt), .eq_in(full_comparator_8_eq),
    .lt_in(full_comparator_8_lt), .gt(full_comparator_11_gt), .eq(full_comparator_11_eq),
    .lt(full_comparator_11_lt));
  full_comparator full_comparator_12 (
    .a(A[8]), .b(B[8]), .gt_in(full_comparator_13_gt), .eq_in(full_comparator_13_eq),
    .lt_in(full_comparator_13_lt), .gt(full_comparator_12_gt), .eq(full_comparator_12_eq),
    .lt(full_comparator_12_lt));
  full_comparator full_comparator_13 (
    .a(A[9]), .b(B[9]), .gt_in(full_comparator_9_gt), .eq_in(full_comparator_9_eq),
    .lt_in(full_comparator_9_lt), .gt(full_comparator_13_gt), .eq(full_comparator_13_eq),
    .lt(full_comparator_13_lt));
  full_comparator full_comparator_14 (
    .a(A[1]), .b(B[1]), .gt_in(full_comparator_10_gt), .eq_in(full_comparator_10_eq),
    .lt_in(full_comparator_10_lt), .gt(full_comparator_14_gt), .eq(full_comparator_14_eq),
    .lt(full_comparator_14_lt));
  full_comparator full_comparator_15 (
    .a(A[0]), .b(B[0]), .gt_in(full_comparator_14_gt), .eq_in(full_comparator_14_eq),
    .lt_in(full_comparator_14_lt), .gt(GT), .eq(EQ), .lt(LT));

  // Other names for the same wires on the sheet: A1 = A[0]; A2 = A[1]; A3 = A[2]; A4 = A[3]; A5 = A[4]; A6 = A[5];
  //   A7 = A[6]; A8 = A[7]; A9 = A[8]; A10 = A[9]; A11 = A[10]; A12 = A[11]; A13 = A[12]; A14 = A[13]; A15 = A[14];
  //   A16 = A[15]; B1 = B[0]; B2 = B[1]; B3 = B[2]; B4 = B[3]; B5 = B[4]; B6 = B[5]; B7 = B[6]; B8 = B[7]; B9 = B[8];
  //   B10 = B[9]; B11 = B[10]; B12 = B[11]; B13 = B[12]; B14 = B[13]; B15 = B[14]; B16 = B[15]
endmodule

module _1bit_upCounter (
  input  clk,
  input  reset,
  output \output 
);

  wire full_adder_1_sum, multiplexer_1_out;

  Multiplexer #(.enable("false")) multiplexer_1 (
    .in0(full_adder_1_sum), .in1(1'b0), .out(multiplexer_1_out), .sel(reset));
  d_flip_flop d_flip_flop_1 (.D(multiplexer_1_out), .clk(clk), .Q(\output ));
  full_adder full_adder_1 (.A(\output ), .B(1'b1), .c_in(1'b0), .sum(full_adder_1_sum));  // open: c_out

  // Notes on the sheet:
  //   1 bit up counter
endmodule

module _2bit_upCounter (
  input  clk,
  input  reset,
  output [1:0] \output 
);

  wire [1:0] multiplexer_1_out, n2bit_adder_1_sum;

  Multiplexer #(.width(2), .enable("false")) multiplexer_1 (
    .in0(n2bit_adder_1_sum), .in1(2'b00), .out(multiplexer_1_out), .sel(reset));
  d_flip_flop d_flip_flop_1 (.D(multiplexer_1_out[1]), .clk(clk), .Q(\output [1]));
  d_flip_flop d_flip_flop_2 (.D(multiplexer_1_out[0]), .clk(clk), .Q(\output [0]));
  _2bit_adder u_2bit_adder_1 (.c_in(1'b0), .A(2'b01), .B(\output ), .sum(n2bit_adder_1_sum));  // open: c_out

  // Notes on the sheet:
  //   2 bit up counter
endmodule
